# Fritzing sketch Buzzer (saved by Fritzing 0.9.6b)
circuit board: 1.35615cm x 2.70769cm
breadboards: 1

parts:
  J1 = Piezo Speaker
  Q1 = PNP-Transistor [package="SOT-23 [SMD]"]
  U1 = ATTINY13 [part_number=ATTiny85 package=so]
  U2 = MPL3115A2 [package=lga8]

nets:
  N1: J1.pin1, Q1.1
  GND: J1.pin2, U1.GND, U2.GND, U2.VDDIO
  VCC: Q1.2, U1.VCC, U2.VDD, U2.CAP
  N2: Q1.0, U1.PB4(ADC2)
  N3: U1.PB0(MOSI), U2.SDA
  N4: U1.PB2(SCK_ADC1), U2.SCL

custom parts:
  MPL3115A2: Altimeter/Pressure Sensor, I2C, 1.95V-3.6V supply, 50 to 110kPa
